# Fritzing sketch circuit (saved by Fritzing 0.9.3b)

parts:
  Adafruit_BNO055_and_BMP280_BFF1 = Adafruit BNO055 and BMP280 BFF [part_number=#5937]  # not connected
  Raspberry_Pi_1 = Raspberry Pi 4 [part_number=RPI-4-b]
  Composant1 = Motor Driver 1A Dual TB6612FNG
  DC_Mot_Enc1 = DC Motor with two-phase hall-encoder [part_number=VT-E-G25A-06-177E]
  J1 = Basic Servo
  S1 = Pushbutton [package="[SMD]"]
  S2 = Toggle Switch [package=THT]
  J2 = Piezo Speaker
  M1 = RPlidar A1M8 [package=THT]
  U1 = TRANSCHIPTC5747 [package=camera_sfv24r-2st_2]  # not connected
  BAT1 = Battery Holders [package=lipo-1100mAh]
  BAT2 = Battery Holders [package=lipo-1100mAh]
  BAT3 = Battery Holders [package=lipo-1100mAh]
  U2 = LuaNode32 / ESP32 [part_number=ESP32S-PIN30]
  U3 = Mini-360 DC-DC Buck converter [package=THT]
  U4 = Mini-360 DC-DC Buck converter [package=THT]
  U5 = Mini-360 DC-DC Buck converter [package=THT]

nets:
  N1: Raspberry_Pi_1.GPIO15, M1.pin7
  N2: Raspberry_Pi_1.GPIO14, M1.pin6
  N3: Composant1.A02, DC_Mot_Enc1.pin6
  N4: Composant1.A01, DC_Mot_Enc1.pin1
  N5: Composant1.VM, U3.OUT+
  N6: Composant1.STBY, U2.D25
  N7: Composant1.BIN1, U2.D26
  N8: Composant1.BIN2, U2.D12
  N9: Composant1.PWMB, U2.D14
  N10: DC_Mot_Enc1.pin3, U2.D33
  N11: DC_Mot_Enc1.pin4, U2.D32
  N12: J1.vcc, U4.OUT+
  N13: J1.pulse, U2.D27
  N14: S1.Pin_3, S1.Pin_4, U2.GND, U2.D19, U3.OUT-
  N15: S2.L1, U5.IN-
  N16: S2.L2, BAT3.-
  N17: J2.pin2, U2.D4
  N18: BAT1.+, U3.IN+
  N19: BAT1.-, BAT2.+
  N20: BAT2.-, BAT3.+
  N21: U2.Vin, U5.OUT+

custom parts:
  Adafruit BNO055 and BMP280 BFF: Our QT Py boards are a great way to make very small microcontroller projects that pack a ton of power - and now we have a way for you to turn many QT Py boards into powerful 9 degree-of-freedom (9DoF) motion plus pressure/altitude sensing projects that are super small! We call this the Adafruit BNO055 + BMP280 BFF—a "Best Friend Forever." When you were a kid, you may have learned about the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
  Raspberry Pi 4: The RPi4, a faster version of the awesome Raspberry Pi 2 B ARM Board with 40 pin gpio. Ready for special Raspberry Pi B+ and RPi2 Hat (Hardware attached (on) top)
  RPlidar A1M8: .The RPLIDAR A1 is the next generation low cost 360 degree 2D laser scanner (LIDAR) solution developed by SLAMTEC. It can take up to 4000 samples of laser ranging per second with high rotation speed. And equipped with SLAMTEC patented OPTMAG technology, it breakouts the life limitation of traditional LIDAR system so as to work stably for a long time.
  LuaNode32 / ESP32: New Image for LuaNode32 DOIT ESP32 DEVKIT V1. Base parts from LuaNode32 / ESP32 ESP32 based LuaNode32 by G.Noorlander DOIT Esp32 DevKit v1 (30 pins long, 11 pins width) by Werner Rothschopf (modified by vanepp Dec 2018)
  Mini-360 DC-DC Buck converter: Mini-360 DC-DC Buck converter. Tiny buck step down voltage converter, input voltage 4.75 to 23V output 1 to 17V adjustable. Available from ebay and the like.

// code stored in the sketch: CIRCUIT.ino

